// Logisim project projeto.circ as structural Verilog
module processador (
  input  [15:0] in_1,
  input  [15:0] in_2,
  input  [15:0] in_3,
  input  [15:0] in_4,
  input  [15:0] in_5,
  input  [15:0] in_6,
  input  [15:0] in_7,
  input  [15:0] in_8,
  input  [15:0] in_9,
  input  [15:0] in_10,
  input  [15:0] in_11,
  input  [15:0] in_12,
  input  [15:0] in_13,
  input  [15:0] in_14,
  input  [15:0] in_15,
  input  [15:0] in_16,
  output [7:0] out_17,
  output [7:0] out_18,
  output [3:0] out_19,
  output [7:0] out_20,
  output [7:0] out_21,
  output [7:0] out_22,
  output [7:0] out_23,
  output [7:0] out_24,
  output [1:0] out_25
);

  wire and_1_out, and_2_out, clock_1_out, comparator_1_eq, control_1_br, control_1_clock_br, control_1_jump,
       control_1_ula, multiplexer_3_out, multiplexer_4_out, not_1_out, not_2_out, not_3_out, or_1_out,
       undriven;
  wire [1:0] adder_1_out, bit_extender_1_out;
  wire [7:0] br_1_rs, br_1_rt, multiplexer_1_out, \ulac_1_saída ;

  or or_1 (or_1_out, control_1_jump, multiplexer_4_out);
  Clock clock_1 (.out(clock_1_out));
  PC pc_1 (
    .Jump_Data(out_21[7:4]), .Jump_Permitir(or_1_out), .Clock(clock_1_out), .in_4(in_1), .in_5(in_2),
    .in_6(in_3), .in_7(in_4), .in_8(in_5), .in_9(in_6), .in_10(in_7), .in_11(in_8), .in_12(in_9),
    .in_13(in_10), .in_14(in_11), .in_15(in_12), .in_16(in_13), .in_17(in_14), .in_18(in_15), .in_19(in_16),
    .out_20(out_19), .Termo(out_21), .Bits(out_23));
  Control control_1 (
    .OP(out_23[7:4]), .Clock(undriven), .ULA(control_1_ula), .Jump(control_1_jump), .BR(control_1_br),
    .Clock_BR(control_1_clock_br));  // open: Clock_RAM, RAM
  assign bit_extender_1_out = {{1{1'b0}}, control_1_ula};  // Bit_Extender bit_extender_1
  not not_1 (not_1_out, out_23[5]);
  BR br_1 (
    .R1(out_23[3:2]), .Cllock(control_1_clock_br), .R2(out_23[1:0]), .\Ativação (control_1_br),
    .Entrada(out_17), .R1_2(out_18), .R2_2(out_20), .R3(out_22), .R4(out_24), .Rs(br_1_rs), .Rt(br_1_rt));
  and and_1 (and_1_out, out_23[4], not_1_out, out_23[6], out_23[7]);
  Multiplexer #(.width(8)) multiplexer_1 (
    .in0(out_21), .in1(br_1_rt), .out(multiplexer_1_out), .sel(out_23[5]));  // open: en
  assign out_25 = {{1{1'b0}}, and_1_out};  // Bit_Extender bit_extender_2
  Adder #(.width(2)) adder_1 (.a(bit_extender_1_out), .b(out_25), .out(adder_1_out));  // open: cin, cout
  ULAC ulac_1 (
    ._1(br_1_rs), ._2(multiplexer_1_out), .OP(out_23[7:4]), .\Saída (\ulac_1_saída ));  // open: out_9, out_10, out_6, out_7, out_4, out_5
  Comparator comparator_1 (.a(br_1_rs), .b(multiplexer_1_out), .eq(comparator_1_eq));  // open: gt, lt
  Multiplexer #(.select(2), .width(8)) multiplexer_2 (
    .in0(out_21), .in1(\ulac_1_saída ), .out(out_17), .sel(adder_1_out));  // open: in2, in3, en
  Multiplexer multiplexer_3 (
    .in0(comparator_1_eq), .in1(not_2_out), .out(multiplexer_3_out), .sel(out_23[4]));  // open: en
  not not_2 (not_2_out, comparator_1_eq);
  not not_3 (not_3_out, out_23[6]);
  and and_2 (and_2_out, out_23[5], not_3_out, out_23[7]);
  Multiplexer multiplexer_4 (
    .in0(1'b0), .in1(multiplexer_3_out), .out(multiplexer_4_out), .sel(and_2_out));  // open: en

  // Notes on the sheet:
  //   Registradores
  //   OP
endmodule

module PC (
  input  [3:0] Jump_Data,
  input  Jump_Permitir,
  input  Clock,
  input  [15:0] in_4,
  input  [15:0] in_5,
  input  [15:0] in_6,
  input  [15:0] in_7,
  input  [15:0] in_8,
  input  [15:0] in_9,
  input  [15:0] in_10,
  input  [15:0] in_11,
  input  [15:0] in_12,
  input  [15:0] in_13,
  input  [15:0] in_14,
  input  [15:0] in_15,
  input  [15:0] in_16,
  input  [15:0] in_17,
  input  [15:0] in_18,
  input  [15:0] in_19,
  output [3:0] out_20,
  output [7:0] Termo,
  output [7:0] Bits
);

  wire not_1_out;

  not not_1 (not_1_out, Jump_Permitir);
  Counter #(.width(4), .max('hf)) counter_1 (
    .load(Jump_Permitir), .D(Jump_Data), .count(not_1_out), .Q(out_20), .clk(Clock));  // open: carry, clr
  Multiplexer #(.select(4), .width(16)) multiplexer_1 (
    .in0(in_4), .in1(in_5), .in2(in_6), .in3(in_7), .in4(in_8), .in5(in_9), .in6(in_10), .in7(in_11),
    .in8(in_12), .in9(in_13), .in10(in_14), .in11(in_15), .in12(in_16), .in13(in_17), .in14(in_18),
    .in15(in_19), .out({Bits, Termo}), .sel(out_20));  // open: en
endmodule

// C
module Control (
  input  [3:0] OP,
  input  Clock,
  output ULA,
  output Jump,
  output BR,
  output Clock_BR,
  output Clock_RAM,
  output RAM
);

  wire demultiplexer_1_out0, demultiplexer_1_out1, demultiplexer_1_out2, demultiplexer_1_out3,
       demultiplexer_1_out4, demultiplexer_1_out5, demultiplexer_1_out6, demultiplexer_1_out7,
       demultiplexer_1_out8, demultiplexer_1_out9, demultiplexer_1_out10, demultiplexer_1_out11,
       demultiplexer_1_out13, demultiplexer_1_out14;

  Demultiplexer #(.select(4)) demultiplexer_1 (
    .out0(demultiplexer_1_out0), .out1(demultiplexer_1_out1), .out2(demultiplexer_1_out2),
    .out3(demultiplexer_1_out3), .out4(demultiplexer_1_out4), .out5(demultiplexer_1_out5),
    .out6(demultiplexer_1_out6), .out7(demultiplexer_1_out7), .out8(demultiplexer_1_out8),
    .out9(demultiplexer_1_out9), .out10(demultiplexer_1_out10), .out11(demultiplexer_1_out11), .out12(Jump),
    .out13(demultiplexer_1_out13), .out14(demultiplexer_1_out14), .out15(RAM), .in(1'b1), .sel(OP));  // open: en
  or or_1 (BR, demultiplexer_1_out13, demultiplexer_1_out14);
  or or_2 (ULA, demultiplexer_1_out2, demultiplexer_1_out3, demultiplexer_1_out4, demultiplexer_1_out5, demultiplexer_1_out6, demultiplexer_1_out7, demultiplexer_1_out8, demultiplexer_1_out9, demultiplexer_1_out10, demultiplexer_1_out11);
  and and_1 (Clock_BR, Clock, BR);
  and and_2 (Clock_RAM, Clock, RAM);
  // also tied to GND on the sheet: {demultiplexer_1_out0, demultiplexer_1_out1}
endmodule

module BR (
  input  \Ativação ,
  input  [7:0] Entrada,
  input  [1:0] R1,
  input  Cllock,
  input  [1:0] R2,
  output [7:0] R1_2,
  output [7:0] Rs,
  output [7:0] R2_2,
  output [7:0] R3,
  output [7:0] Rt,
  output [7:0] R4
);

  wire demultiplexer_1_out0, demultiplexer_1_out1, demultiplexer_1_out2, demultiplexer_1_out3,
       multiplexer_1_out, not_1_out, not_2_out;

  not not_1 (not_1_out, Cllock);
  not not_2 (not_2_out, \Ativação );
  Demultiplexer #(.select(2)) demultiplexer_1 (
    .out0(demultiplexer_1_out0), .out1(demultiplexer_1_out1), .out2(demultiplexer_1_out2),
    .out3(demultiplexer_1_out3), .in(multiplexer_1_out), .sel(R1));  // open: en
  Multiplexer #(.disabled(0)) multiplexer_1 (
    .in0(not_1_out), .in1(1'b0), .out(multiplexer_1_out), .sel(not_2_out));  // open: en
  Register register_1 (.D(Entrada), .Q(R1_2), .clk(demultiplexer_1_out0));  // open: en, clr
  Register register_2 (.D(Entrada), .Q(R2_2), .clk(demultiplexer_1_out1));  // open: en, clr
  Register register_3 (.D(Entrada), .Q(R3), .clk(demultiplexer_1_out2));  // open: en, clr
  Register register_4 (.D(Entrada), .Q(R4), .clk(demultiplexer_1_out3));  // open: en, clr
  Multiplexer #(.select(2), .width(8)) multiplexer_2 (
    .in0(R1_2), .in1(R2_2), .in2(R3), .in3(R4), .out(Rs), .sel(R1));  // open: en
  Multiplexer #(.select(2), .width(8)) multiplexer_3 (
    .in0(R1_2), .in1(R2_2), .in2(R3), .in3(R4), .out(Rt), .sel(R2));  // open: en
endmodule

// ULA
module ULAC (
  input  [3:0] OP,
  input  [7:0] _1,
  input  [7:0] _2,
  output [7:0] out_4,
  output [7:0] out_5,
  output [7:0] out_6,
  output [7:0] out_7,
  output [7:0] \Saída ,
  output [7:0] out_9,
  output [7:0] out_10
);

  assign out_4 = _1 & _2;  // AND_Gate and_1, 8 bits wide
  assign out_5 = _1 | _2;  // OR_Gate or_1, 8 bits wide
  assign out_6 = ~(_1 & _2);  // NAND_Gate nand_1, 8 bits wide
  assign out_7 = ~(_1 | _2);  // NOR_Gate nor_1, 8 bits wide
  Adder adder_1 (.a(_1), .b(_2), .out(out_9));  // open: cin, cout
  Subtractor subtractor_1 (.a(_1), .b(_2), .out(out_10));  // open: bin, bout
  Multiplexer #(.select(4), .width(8)) multiplexer_1 (
    .in0({8{1'b0}}), .in1({8{1'b0}}), .in2(out_4), .in3(out_5), .in4(out_6), .in5(out_7), .in6(out_9),
    .in7(out_10), .in8(out_9), .in9(out_10), .in10({8{1'b0}}), .in11({8{1'b0}}), .in12({8{1'b0}}),
    .in13({8{1'b0}}), .in14({8{1'b0}}), .in15({8{1'b0}}), .out(\Saída ), .sel(OP));  // open: en
endmodule

module ula (
  input  [3:0] op,
  input  [7:0] _1,
  input  [7:0] _2,
  output [7:0] \Saída ,
  output \Saída_2 
);

  wire and_1_out, comparator_1_eq, multiplexer_2_out, not_1_out, not_2_out;

  Comparator comparator_1 (.a(_1), .b(_2), .eq(comparator_1_eq));  // open: gt, lt
  ULAC ulac_1 (._1(_1), ._2(_2), .OP(op), .\Saída (\Saída ));  // open: out_9, out_10, out_6, out_7, out_4, out_5
  not not_1 (not_1_out, comparator_1_eq);
  not not_2 (not_2_out, op[2]);
  Multiplexer multiplexer_1 (.in0(1'b0), .in1(multiplexer_2_out), .out(\Saída_2 ), .sel(and_1_out));  // open: en
  Multiplexer multiplexer_2 (.in0(comparator_1_eq), .in1(not_1_out), .out(multiplexer_2_out), .sel(op[0]));  // open: en
  and and_1 (and_1_out, op[1], not_2_out, op[3]);
endmodule

module processador_v2 (
  input  [15:0] in_1,
  input  [15:0] in_2,
  input  [15:0] in_3,
  input  [15:0] in_4,
  input  [15:0] in_5,
  input  [15:0] in_6,
  input  [15:0] in_7,
  input  [15:0] in_8,
  input  [15:0] in_9,
  input  [15:0] in_10,
  input  [15:0] in_11,
  input  [15:0] in_12,
  input  [15:0] in_13,
  input  [15:0] in_14,
  input  [15:0] in_15,
  input  [15:0] in_16,
  output [7:0] out_17,
  output [7:0] out_18,
  output [3:0] out_19,
  output [7:0] out_20,
  output [7:0] out_21,
  output [7:0] out_22,
  output [7:0] out_23,
  output [7:0] out_24,
  output [7:0] out_25,
  output [7:0] out_26,
  output [7:0] out_27
);

  wire clock_1_out, control_v2_1_br, control_v2_1_clock_br, control_v2_1_clock_ram, control_v2_1_jump,
       control_v2_1_ram, not_1_out, or_1_out, pre_seletor_1_sinal_ram, pre_seletor_1_sinal_ula,
       \ula_1_saída_2 ;
  wire [7:0] multiplexer_1_out, ram_1_data;

  or or_1 (or_1_out, \ula_1_saída_2 , control_v2_1_jump);
  Clock clock_1 (.out(clock_1_out));
  PC pc_1 (
    .Jump_Data(out_20[7:4]), .Jump_Permitir(or_1_out), .Clock(clock_1_out), .in_4(in_1), .in_5(in_2),
    .in_6(in_3), .in_7(in_4), .in_8(in_5), .in_9(in_6), .in_10(in_7), .in_11(in_8), .in_12(in_9),
    .in_13(in_10), .in_14(in_11), .in_15(in_12), .in_16(in_13), .in_17(in_14), .in_18(in_15), .in_19(in_16),
    .out_20(out_19), .Termo(out_20), .Bits(out_21));
  Control_v2 control_v2_1 (
    .OP(out_21[7:4]), .Clock(clock_1_out), .Jump(control_v2_1_jump), .BR(control_v2_1_br),
    .Clock_BR(control_v2_1_clock_br), .Clock_RAM(control_v2_1_clock_ram), .RAM(control_v2_1_ram));  // open: ULA
  not not_1 (not_1_out, control_v2_1_ram);
  BR br_1 (
    .R1(out_21[3:2]), .Cllock(control_v2_1_clock_br), .R2(out_21[1:0]), .\Ativação (control_v2_1_br),
    .Entrada(out_17), .R1_2(out_22), .R2_2(out_23), .R3(out_24), .R4(out_25), .Rs(out_26), .Rt(out_27));
  RAM_part ram_1 (.addr(out_20), .data(ram_1_data), .clk(control_v2_1_clock_ram), .ld(not_1_out));  // open: sel, clr
  pre_seletor pre_seletor_1 (
    .op(out_21[7:4]), .sinal_ula(pre_seletor_1_sinal_ula), .sinal_ram(pre_seletor_1_sinal_ram));
  Multiplexer #(.width(8)) multiplexer_1 (
    .in0(out_20), .in1(out_27), .out(multiplexer_1_out), .sel(out_21[5]));  // open: en
  assign ram_1_data = control_v2_1_ram ? out_26 : 8'bz;  // Controlled_Buffer controlled_buffer_1
  seletor_de_entrada seletor_de_entrada_1 (
    .sinal_ula(pre_seletor_1_sinal_ula), .sinal_ram(pre_seletor_1_sinal_ram), .\Saída (out_17),
    .termo(out_20), .ula(out_18), .ram(ram_1_data));
  ula ula_1 (._1(out_26), ._2(multiplexer_1_out), .op(out_21[7:4]), .\Saída (out_18), .\Saída_2 (\ula_1_saída_2 ));
endmodule

// UC
module Control_v2 (
  input  [3:0] OP,
  input  Clock,
  output ULA,
  output Jump,
  output BR,
  output Clock_BR,
  output Clock_RAM,
  output RAM
);

  wire and_1_out, and_3_out, demultiplexer_1_out0, demultiplexer_1_out1, demultiplexer_1_out2,
       demultiplexer_1_out3, demultiplexer_1_out4, demultiplexer_1_out5, demultiplexer_1_out6,
       demultiplexer_1_out7, demultiplexer_1_out8, demultiplexer_1_out9, demultiplexer_1_out10,
       demultiplexer_1_out11, demultiplexer_1_out13, demultiplexer_1_out14, not_1_out, not_2_out, or_1_out;

  Demultiplexer #(.select(4)) demultiplexer_1 (
    .out0(demultiplexer_1_out0), .out1(demultiplexer_1_out1), .out2(demultiplexer_1_out2),
    .out3(demultiplexer_1_out3), .out4(demultiplexer_1_out4), .out5(demultiplexer_1_out5),
    .out6(demultiplexer_1_out6), .out7(demultiplexer_1_out7), .out8(demultiplexer_1_out8),
    .out9(demultiplexer_1_out9), .out10(demultiplexer_1_out10), .out11(demultiplexer_1_out11), .out12(Jump),
    .out13(demultiplexer_1_out13), .out14(demultiplexer_1_out14), .out15(RAM), .in(1'b1), .sel(OP));  // open: en
  or or_1 (or_1_out, demultiplexer_1_out13, demultiplexer_1_out14);
  or or_2 (ULA, demultiplexer_1_out2, demultiplexer_1_out3, demultiplexer_1_out4, demultiplexer_1_out5, demultiplexer_1_out6, demultiplexer_1_out7, demultiplexer_1_out8, demultiplexer_1_out9, demultiplexer_1_out10, demultiplexer_1_out11);
  and and_1 (and_1_out, Clock, or_1_out);
  and and_2 (Clock_RAM, Clock, RAM);
  not not_1 (not_1_out, demultiplexer_1_out10);
  and and_3 (and_3_out, ULA, not_1_out, not_2_out);
  not not_2 (not_2_out, demultiplexer_1_out11);
  or or_3 (BR, and_3_out, or_1_out);
  or or_4 (Clock_BR, and_3_out, and_1_out);
  // also tied to GND on the sheet: {demultiplexer_1_out0, demultiplexer_1_out1}
endmodule

// sel
module seletor_de_entrada (
  input  sinal_ula,
  input  sinal_ram,
  input  [7:0] termo,
  input  [7:0] ula,
  input  [7:0] ram,
  output [7:0] \Saída 
);

  wire multiplexer_1_out;
  wire [1:0] adder_1_out, bit_extender_1_out, bit_extender_2_out;

  Multiplexer multiplexer_1 (.in0(sinal_ula), .in1(sinal_ram), .out(multiplexer_1_out), .sel(sinal_ram));  // open: en
  assign bit_extender_1_out = {{1{1'b0}}, multiplexer_1_out};  // Bit_Extender bit_extender_1
  assign bit_extender_2_out = {{1{1'b0}}, sinal_ram};  // Bit_Extender bit_extender_2
  Adder #(.width(2)) adder_1 (.a(bit_extender_1_out), .b(bit_extender_2_out), .out(adder_1_out));  // open: cin, cout
  Multiplexer #(.select(2), .width(8)) multiplexer_2 (
    .in0(termo), .in1(ula), .in2(ram), .in3({8{1'b0}}), .out(\Saída ), .sel(adder_1_out));  // open: en
endmodule

module pre_seletor (
  input  [3:0] op,
  output sinal_ula,
  output sinal_ram
);

  wire and_1_out, not_1_out, not_2_out, not_3_out;

  not not_1 (not_1_out, op[0]);
  and and_1 (and_1_out, not_1_out, op[1], op[2], op[3]);
  not not_2 (not_2_out, op[1]);
  and and_2 (sinal_ram, op[0], not_2_out, op[2], op[3]);
  not not_3 (not_3_out, and_1_out);
  Multiplexer #(.select(4)) multiplexer_1 (
    .in0(1'b0), .in1(not_3_out), .in2(not_3_out), .in3(not_3_out), .in4(not_3_out), .in5(not_3_out),
    .in6(not_3_out), .in7(not_3_out), .in8(not_3_out), .in9(not_3_out), .in10(not_3_out), .in11(not_3_out),
    .in12(not_3_out), .in13(not_3_out), .in14(not_3_out), .in15(not_3_out), .out(sinal_ula), .sel(op));  // open: en
endmodule
